# Fritzing sketch ContorlSurfaceMainsButtonsBup (saved by Fritzing 0.9.5d)
breadboards: 1

parts:
  Play = Pushbutton [package="[THT]"]
  Stop = Pushbutton [package="[THT]"]
  Record = Pushbutton [package="[THT]"]
  Insert_Marker = Pushbutton [package="[THT]"]
  Rewind = Pushbutton [package="[THT]"]
  FF = Pushbutton [package="[THT]"]
  Loop = Pushbutton [package="[THT]"]
  Delete_Marker = Pushbutton [package="[THT]"]
  up = Pushbutton [package="[THT]"]  # not connected
  Down = Pushbutton [package="[THT]"]  # not connected
  Right = Pushbutton [package="[THT]"]
  Left = Pushbutton [package="[THT]"]
  Option = Pushbutton [package="[THT]"]
  Shift = Pushbutton [package="[THT]"]  # not connected
  incP = Pushbutton [package="[THT]"]
  IncMin = Pushbutton [package="[THT]"]

nets:
  N1: Play.Pin_1, Play.Pin_2, Stop.Pin_3, Stop.Pin_4, Record.Pin_1, Record.Pin_2
  N2: Stop.Pin_1, Stop.Pin_2
  N3: Insert_Marker.Pin_1, Insert_Marker.Pin_2
  N4: Insert_Marker.Pin_3, Insert_Marker.Pin_4
  N5: Rewind.Pin_1, Rewind.Pin_2, FF.Pin_3, FF.Pin_4, Loop.Pin_1, Loop.Pin_2
  N6: Rewind.Pin_3, Rewind.Pin_4
  N7: FF.Pin_1, FF.Pin_2
  N8: Delete_Marker.Pin_1, Delete_Marker.Pin_2
  N9: Delete_Marker.Pin_3, Delete_Marker.Pin_4
  N10: Right.Pin_3, Right.Pin_4, Left.Pin_3, IncMin.Pin_1, IncMin.Pin_2
  N11: Option.Pin_1, Option.Pin_2
  N12: Option.Pin_3, Option.Pin_4
  N13: incP.Pin_1, incP.Pin_2
  N14: incP.Pin_3, incP.Pin_4
  N15: IncMin.Pin_3, IncMin.Pin_4

notes:
  Still need
  Shift
  FFwd
