# Fritzing sketch Control Surface Prototype v2 No EXT Items (saved by Fritzing 0.9.5d)
circuit board: 8.46667cm x 5.64444cm
breadboards: 2

parts:
  S1 = Pushbutton [part_number=Mute package="[THT]"]
  Part2 = Arduino Nano (Rev3.0) (ICSP)
  U2 = Molex Picoblade Series Header [part_number=0533980471 package=Picoblade-53398-0471]  # not connected
  U3 = Molex Picoblade Series Header [part_number=0533980571 package=Picoblade-53398-0571]  # not connected
  U8 = Molex Picoblade Series Header [part_number=0533980371 package=Picoblade-53398-0371]  # not connected
  S4 = Momentary Switch [part_number=Select package=ksa_sealed_tac_switch]
  S2 = Momentary Switch [part_number=Solo package=ksa_sealed_tac_switch]
  S3 = Momentary Switch [part_number=RecReady package=ksa_sealed_tac_switch]
  U9 = SLIDER [package=slider]  # not connected
  U10 = POT [package=pot_mammoth]  # not connected
  S5 = Pushbutton [part_number=Mute package="[THT]"]
  S6 = Pushbutton [part_number=Mute package="[THT]"]
  S7 = Pushbutton [part_number=Mute package="[THT]"]
  S8 = Pushbutton [part_number=Mute package="[THT]"]
  S9 = Pushbutton [part_number=Mute package="[THT]"]
  S10 = Pushbutton [part_number=Mute package="[THT]"]
  S11 = Pushbutton [part_number=Mute package="[THT]"]
  S12 = Pushbutton [part_number=Mute package="[THT]"]
  S13 = Pushbutton [part_number=Mute package="[THT]"]
  M1 = DOIT Esp32 DevKit v1 (30 pins long, 11 pins width) [part_number=ESP32S-PIN30]
  JACK2 = 2.1mm Barrel Jack with Terminal Block
  JACK1 = 2.1mm Barrel Jack with Terminal Block
  VCC1 = Battery

nets (from the breadboard view):
  N1: S1.Pin_1, S1.Pin_2, S1.Pin_3, S1.Pin_4, S4.1, S4.3, S2.2, S2.4, S3.2, S3.4, M1.GND
  N2: Part2.GND, JACK2.POS, JACK2.NEG
  N3: S5.Pin_1, S5.Pin_2
  N4: S5.Pin_3, S5.Pin_4
  N5: S6.Pin_1, S6.Pin_2
  N6: S6.Pin_3, S6.Pin_4
  N7: S7.Pin_1, S7.Pin_2
  N8: S7.Pin_3, S7.Pin_4
  N9: S8.Pin_1, S8.Pin_2
  N10: S8.Pin_3, S8.Pin_4
  N11: S9.Pin_1, S9.Pin_2
  N12: S9.Pin_3, S9.Pin_4
  N13: S10.Pin_1, S10.Pin_2
  N14: S10.Pin_3, S10.Pin_4
  N15: S11.Pin_1, S11.Pin_2
  N16: S11.Pin_3, S11.Pin_4
  N17: S12.Pin_1, S12.Pin_2
  N18: S12.Pin_3, S12.Pin_4
  N19: S13.Pin_1, S13.Pin_2
  N20: S13.Pin_3, S13.Pin_4
  N21: JACK1.POS, VCC1.+
  N22: JACK1.NEG, VCC1.-

notes:
  Mute
  Solo
  Record Ready
  Select
  Balance
  High Current
  Main Fader
  Main Mute (with light)
  High Voltage
  Low Voltage
  XY Pad
  Transport Buttons
  Mains Strip

custom parts:
  DOIT Esp32 DevKit v1 (30 pins long, 11 pins width): The DOIT Esp32 DevKit v1 is one of the development board created by DOIT to evaluate the ESP-WROOM-32 module. It is based on the ESP32 microcontroller that boasts Wifi, Bluetooth, Ethernet and Low Power support all in a single chip. (vanepp) made breadboard work, adjusted pin numbering and labels and reduced size of schematic and cleaned up pcb. This chip is 30pins long (2 x15) and 11 pins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
  Battery: Your standard 2x 18650 battery pack (7,4 Volts)
