# Fritzing sketch Control Surface Prototype v2 (saved by Fritzing 0.9.5d)
circuit board: 8.46667cm x 5.64444cm
breadboards: 2

parts:
  S1 = Pushbutton [part_number=Mute package="[THT]"]
  Grove1 = Grove OLED 128x96
  Part2 = Arduino Nano (Rev3.0) (ICSP)
  Part3 = Thumb Joystick
  U2 = Molex Picoblade Series Header [part_number=0533980471 package=Picoblade-53398-0471]  # not connected
  U3 = Molex Picoblade Series Header [part_number=0533980571 package=Picoblade-53398-0571]  # not connected
  U4 = Molex Picoblade Series Header [part_number=0533980471 package=Picoblade-53398-0471]
  U5 = Molex Picoblade Series Header [part_number=0533980571 package=Picoblade-53398-0571]
  neopixel1 = Neopixel Ring 12
  U7 = Molex Picoblade Series Header [part_number=0533980371 package=Picoblade-53398-0371]
  U8 = Molex Picoblade Series Header [part_number=0533980371 package=Picoblade-53398-0371]  # not connected
  S4 = Momentary Switch [part_number=Select package=ksa_sealed_tac_switch]
  S2 = Momentary Switch [part_number=Solo package=ksa_sealed_tac_switch]
  S3 = Momentary Switch [part_number=RecReady package=ksa_sealed_tac_switch]
  U9 = SLIDER [package=slider]  # not connected
  U10 = POT [package=pot_mammoth]  # not connected
  U11 = SLIDER [package=slider]  # not connected
  S5 = Pushbutton [part_number=Mute package="[THT]"]
  S6 = Pushbutton [part_number=Mute package="[THT]"]
  S7 = Pushbutton [part_number=Mute package="[THT]"]
  S8 = Pushbutton [part_number=Mute package="[THT]"]
  S9 = Pushbutton [part_number=Mute package="[THT]"]
  S10 = Pushbutton [part_number=Mute package="[THT]"]
  S11 = Pushbutton [part_number=Mute package="[THT]"]
  S12 = Pushbutton [part_number=Mute package="[THT]"]
  S13 = Pushbutton [part_number=Mute package="[THT]"]
  neopixel2 = Neopixel Ring 12
  U12 = Molex Picoblade Series Header [part_number=0533980371 package=Picoblade-53398-0371]
  neopixel3 = Neopixel Ring 12
  U13 = Molex Picoblade Series Header [part_number=0533980371 package=Picoblade-53398-0371]
  EDGY_motor_control1 = EDGY  # not connected
  JACK1 = 2.1mm Barrel Jack with Terminal Block
  VCC1 = Battery
  JACK2 = 2.1mm Barrel Jack with Terminal Block
  M1 = DOIT Esp32 DevKit v1 (30 pins long, 11 pins width) [part_number=ESP32S-PIN30]

nets (from the breadboard view):
  N1: S1.Pin_1, S1.Pin_2, S1.Pin_3, S1.Pin_4, S4.1, S4.3, S2.2, S2.4, S3.2, S3.4, M1.GND
  N2: Grove1.GND, U4.1
  N3: Grove1.VCC, U4.2
  N4: Grove1.SDA, U4.3
  N5: Grove1.SCL, U4.4
  N6: Part2.GND, JACK2.POS, JACK2.NEG
  N7: Part3.GND, U5.1
  N8: Part3.SEL, U5.2
  N9: Part3.HORZ, U5.3
  N10: Part3.VERT, U5.4
  N11: Part3.VCC, U5.5
  N12: neopixel1.GND, U7.2
  N13: neopixel1.VCC, U7.1
  N14: neopixel1.IN, U7.3
  N15: S5.Pin_1, S5.Pin_2
  N16: S5.Pin_3, S5.Pin_4
  N17: S6.Pin_1, S6.Pin_2
  N18: S6.Pin_3, S6.Pin_4
  N19: S7.Pin_1, S7.Pin_2
  N20: S7.Pin_3, S7.Pin_4
  N21: S8.Pin_1, S8.Pin_2
  N22: S8.Pin_3, S8.Pin_4
  N23: S9.Pin_1, S9.Pin_2
  N24: S9.Pin_3, S9.Pin_4
  N25: S10.Pin_1, S10.Pin_2
  N26: S10.Pin_3, S10.Pin_4
  N27: S11.Pin_1, S11.Pin_2
  N28: S11.Pin_3, S11.Pin_4
  N29: S12.Pin_1, S12.Pin_2
  N30: S12.Pin_3, S12.Pin_4
  N31: S13.Pin_1, S13.Pin_2
  N32: S13.Pin_3, S13.Pin_4
  N33: neopixel2.GND, U12.2
  N34: neopixel2.VCC, U12.1
  N35: neopixel2.IN, U12.3
  N36: neopixel3.GND, U13.2
  N37: neopixel3.VCC, U13.1
  N38: neopixel3.IN, U13.3
  N39: JACK1.POS, VCC1.+
  N40: JACK1.NEG, VCC1.-

notes:
  High Current
  Mute
  Solo
  Record Ready
  Select
  Balance
  Main Fader
  Main Mute (with light)
  High Voltage
  Low Voltage
  XY Pad
  Transport Buttons
  Mains Strip

custom parts:
  Neopixel Ring 12: Neopixel Ring x12
  Battery: Your standard 2x 18650 battery pack (7,4 Volts)
  DOIT Esp32 DevKit v1 (30 pins long, 11 pins width): The DOIT Esp32 DevKit v1 is one of the development board created by DOIT to evaluate the ESP-WROOM-32 module. It is based on the ESP32 microcontroller that boasts Wifi, Bluetooth, Ethernet and Low Power support all in a single chip. (vanepp) made breadboard work, adjusted pin numbering and labels and reduced size of schematic and cleaned up pcb. This chip is 30pins long (2 x15) and 11 pins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
