# Fritzing sketch Control Surface Prototype (saved by Fritzing 0.9.5d)
circuit board: 8.46667cm x 5.64444cm
breadboards: 2

parts:
  S1 = Pushbutton [package="[THT]"]
  S2 = Momentary Switch [package=ksa_sealed_tac_switch]
  S3 = Momentary Switch [package=ksa_sealed_tac_switch]
  S4 = Momentary Switch [package=ksa_sealed_tac_switch]
  R1 = Rotary Potentiometer (Small) [maximum_resistance=100kΩ package=THT]
  R2 = Rotary Potentiometer (Small) [maximum_resistance=100kΩ package=THT]
  Grove1 = Grove OLED 128x96
  CPU1 = NodeMCU WROOM ESP 32
  S5 = Pushbutton [package="[THT]"]
  S6 = Momentary Switch [package=ksa_sealed_tac_switch]
  S7 = Momentary Switch [package=ksa_sealed_tac_switch]
  S8 = Momentary Switch [package=ksa_sealed_tac_switch]
  U1 = ENCODER-QUADRATURE [package=encoder-16mm-quad]
  Grove2 = Grove OLED 128x96  # not connected
  S11 = Pushbutton [package="[THT]"]
  S12 = Pushbutton [package="[THT]"]
  S13 = Pushbutton [package="[THT]"]
  S14 = Pushbutton [package="[THT]"]
  R5 = Rotary Potentiometer (Small) [maximum_resistance=100kΩ package=THT]
  R6 = Rotary Potentiometer (Small) [maximum_resistance=100kΩ package=THT]
  Part2 = Arduino Nano (Rev3.0) (ICSP)
  Part3 = Thumb Joystick
  U2 = Molex Picoblade Series Header [part_number=0533980471 package=Picoblade-53398-0471]
  U3 = Molex Picoblade Series Header [part_number=0533980571 package=Picoblade-53398-0571]
  U4 = Molex Picoblade Series Header [part_number=0533980471 package=Picoblade-53398-0471]
  U5 = Molex Picoblade Series Header [part_number=0533980571 package=Picoblade-53398-0571]
  neopixel1 = Neopixel Ring 12
  U7 = Molex Picoblade Series Header [part_number=0533980371 package=Picoblade-53398-0371]
  U8 = Molex Picoblade Series Header [part_number=0533980371 package=Picoblade-53398-0371]

nets:
  N1: S1.Pin_1, S1.Pin_2
  N2: S1.Pin_3, S1.Pin_4, S2.4, S3.4, S4.4, R1.leg1, R2.leg1, CPU1.pin_15, S6.3, S6.4, S7.4, S8.4, U1.B
  N3: S2.2, CPU1.pin_13
  N4: S3.2, CPU1.pin_12
  N5: S4.2, CPU1.pin_11
  N6: R1.wiper, CPU1.pin_10
  N7: R1.leg2, R2.leg2, CPU1.pin_17, U3.5
  N8: R2.wiper, CPU1.pin_9, CPU1.pin_25
  N9: Grove1.GND, U4.1
  N10: Grove1.VCC, U4.2
  N11: Grove1.SDA, U4.3
  N12: Grove1.SCL, U4.4
  N13: CPU1.pin_3, S5.Pin_1, S5.Pin_2
  N14: CPU1.pin_4, U1.A
  N15: CPU1.pin_5, U1.C
  N16: CPU1.pin_6, S7.2
  N17: CPU1.pin_7, S6.1, S6.2
  N18: CPU1.pin_8, CPU1.pin_24, S8.2, U8.3
  N19: CPU1.pin_19, U3.4
  N20: CPU1.pin_21, U3.3
  N21: CPU1.pin_22, U3.2
  N22: CPU1.pin_23, S11.Pin_3, S11.Pin_4, S12.Pin_3, S12.Pin_4, S13.Pin_3, S13.Pin_4, S14.Pin_3, S14.Pin_4, R5.leg1, R6.leg1
  N23: CPU1.pin_26, R5.wiper
  N24: CPU1.pin_27, U2.4
  N25: CPU1.pin_30, U2.3
  N26: CPU1.pin_31, R6.wiper
  N27: S5.Pin_3, S5.Pin_4, Part2.GND, U2.1, U3.1, U8.1
  N28: S11.Pin_1, S11.Pin_2
  N29: S12.Pin_1, S12.Pin_2
  N30: S13.Pin_1, S13.Pin_2
  N31: S14.Pin_1, S14.Pin_2
  N32: R5.leg2, R6.leg2
  N33: Part3.GND, U5.1
  N34: Part3.SEL, U5.2
  N35: Part3.HORZ, U5.3
  N36: Part3.VERT, U5.4
  N37: Part3.VCC, U5.5
  N38: U2.2, U8.2
  N39: neopixel1.GND, U7.2
  N40: neopixel1.VCC, U7.1
  N41: neopixel1.IN, U7.3

notes:
  High Current

custom parts:
  NodeMCU WROOM ESP 32: 30 pol Development Kit
  Neopixel Ring 12: Neopixel Ring x12
