# Fritzing sketch Transport (saved by Fritzing 0.9.5d)
circuit board: 8.46667cm x 5.64444cm
perfboards: 1

parts:
  S3 = Momentary Switch [package=ksa_sealed_tac_switch]
  S4 = Momentary Switch [package=ksa_sealed_tac_switch]
  S5 = Momentary Switch [package=ksa_sealed_tac_switch]
  S6 = Momentary Switch [package=ksa_sealed_tac_switch]
  S7 = Momentary Switch [package=ksa_sealed_tac_switch]
  S8 = Momentary Switch [package=ksa_sealed_tac_switch]
  S9 = Momentary Switch [package=ksa_sealed_tac_switch]
  S10 = Momentary Switch [package=ksa_sealed_tac_switch]
  JP2 = Header 4 [package=molex-1x4_lock]
  JP3 = Header 6 [package=molex-1x6-ra]

nets:
  N1: S3.2, S4.1, S5.2, S6.1, S8.1, S10.2, JP3.5
  N2: S3.3, JP3.2
  N3: S4.4, JP2.4
  N4: S5.3, JP3.1
  N5: S6.4, JP2.3
  N6: S7.1, S9.2
  N7: S7.3, JP2.2
  N8: S8.3, JP2.1
  N9: S9.4, JP3.3
  N10: S10.4, JP3.4
